# Fritzing sketch osvaldo (saved by Fritzing 0.9.3b)

parts:
  XIAO_ESP32S1 = XIAO ESP32S3 [package="DIP (Dual Inline) [THT]"]  # not connected
  Grove_Shield_for_XIAO_1 = Grove Shield for XIAO [package="DIP (Dual Inline) [THT]"]
  Part1 = Thermal Printer
  Grove_Shield_for_XIAO_2 = Grove Shield for XIAO [package="DIP (Dual Inline) [THT]"]
  XIAO_ESP32S2 = XIAO ESP32S3 [package="DIP (Dual Inline) [THT]"]
  U1 = Mini-360 DC-DC Buck converter [package=THT]
  J1 = Power Jack [package=power_jack_smd]
  U2 = SWITCH_SPDT [package=kps-1290]
  D1 = Rectifier Diode [part_number=1N4001 package="300 mil [THT]"]
  D2 = Rectifier Diode [part_number=1N4001 package="300 mil [THT]"]
  RGB_SMD_LED1 = SMD RGB LED (WS2812) [package=5050]
  RGB_SMD_LED5 = SMD RGB LED (WS2812) [package=5050]
  U3 = SWITCH_SPDT [package=kps-1290]

nets:
  N1: Grove_Shield_for_XIAO_1.GND#25, Grove_Shield_for_XIAO_2.GND#25, U1.OUT-
  N2: Grove_Shield_for_XIAO_1.5V#27, D2.cathode
  N3: Grove_Shield_for_XIAO_1.GND#30, RGB_SMD_LED5.DOut
  N4: Grove_Shield_for_XIAO_1.3V3#31, RGB_SMD_LED5.VCC
  N5: Grove_Shield_for_XIAO_1.0, RGB_SMD_LED1.DIn
  N6: Grove_Shield_for_XIAO_1.GND#34, RGB_SMD_LED1.DOut
  N7: Grove_Shield_for_XIAO_1.3V3#35, RGB_SMD_LED1.VCC
  N8: Grove_Shield_for_XIAO_1.1, RGB_SMD_LED5.DIn
  N9: Grove_Shield_for_XIAO_1.SDA4, Part1.RXD
  N10: Grove_Shield_for_XIAO_1.SCL5, Part1.TXD
  N11: Grove_Shield_for_XIAO_1.GND#42, Grove_Shield_for_XIAO_2.GND#42
  N12: Part1.GND#0, U1.IN-, J1.GND
  N13: Part1.VH, U1.IN+, U2.P
  N14: Grove_Shield_for_XIAO_2.0, XIAO_ESP32S2.D0
  N15: Grove_Shield_for_XIAO_2.1, XIAO_ESP32S2.D1
  N16: Grove_Shield_for_XIAO_2.2, XIAO_ESP32S2.D2
  N17: Grove_Shield_for_XIAO_2.3, XIAO_ESP32S2.D3
  N18: Grove_Shield_for_XIAO_2.4, XIAO_ESP32S2.D4
  N19: Grove_Shield_for_XIAO_2.5, XIAO_ESP32S2.D5
  N20: Grove_Shield_for_XIAO_2.6, XIAO_ESP32S2.D6
  N21: Grove_Shield_for_XIAO_2.7, XIAO_ESP32S2.D7
  N22: Grove_Shield_for_XIAO_2.8, XIAO_ESP32S2.D8
  N23: Grove_Shield_for_XIAO_2.9, XIAO_ESP32S2.D9
  N24: Grove_Shield_for_XIAO_2.10, XIAO_ESP32S2.D10
  3V3: Grove_Shield_for_XIAO_2.3V3, XIAO_ESP32S2.3V3
  N25: Grove_Shield_for_XIAO_2.GND#24, XIAO_ESP32S2.GND
  N26: Grove_Shield_for_XIAO_2.5V#26, XIAO_ESP32S2.5V
  N27: Grove_Shield_for_XIAO_2.5V#27, D1.cathode
  N28: U1.OUT+, U3.S
  N29: J1.GNDBREAK, U2.O, D1.anode
  N30: D2.anode, U3.P

custom parts:
  XIAO ESP32S3: Seeed Studio XIAO ESP32S3 leverages 240MHz Xtensa 32-bit LX7 dual-core processor, supporting both WiFi and BLE 5.0 wireless connectivities, a 2.4GHz Rod antenna, allows for deep sleep mode with power consumption as low as 14μA while supporting lithium battery charging management. Ideal for the Internet of Things, Smart Homes, Wireless wearable devices, Robotics, etc.
  Grove Shield for XIAO: Seeed Studio Grove Base for XIAO is a plug-and-play Grove extension board for Seeed Studio XIAO. With the on-board battery management chip and battery bonding pad, you could easily power your Seeed Studio XIAO with lithium battery and recharge it. 8 Grove connectors onboard includes two Grove I2C and one UART. It acts as a bridge for Seeed Studio XIAO and Seeed's Grove system. Flash SPI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
  Mini-360 DC-DC Buck converter: Mini-360 DC-DC Buck converter. Tiny buck step down voltage converter, input voltage 4.75 to 23V output 1 to 17V adjustable. Available from ebay and the like.
